// Logisim project MY_16BIT_CPU.circ as structural Verilog: 13 circuits, main circuit main
module main (
  input  in_1,
  input  in_2,
  input  RAM_READ,
  input  in_4,
  input  [3:0] in_5,
  input  KB_REG_OUT,
  input  in_7
);

  wire ACC_READ, ADD, alu_1_carry_flag, alu_1_negative_flag, alu_1_zero_flag, button_1_out, CARRY,
       clk_1_clock_out, clock_1_out, CMP, CTN_ENB, CTN_OUT, decoder_1_out6, INSTRUCT_READ, KB_REG_READ,
       MAR_READ, NEGATIVE, not_1_out, or_1_out, RAM_READ_t, READ_B, READ_X, READ_Y, STACK_DATA_READ,
       STACK_UP, SUB, undriven, UPPER_BITS_READ, ZERO;
  wire [2:0] step_counter_1_data_out;
  wire [3:0] dipswitch_2_sw3;
  wire [3:3] step_counter_1_data_out_2;
  wire [6:0] keyboard_1_data;
  wire [7:0] frame_buffer_1_out_9, frame_buffer_1_out_10, frame_buffer_1_out_11, frame_buffer_1_out_12,
       frame_buffer_1_out_13, frame_buffer_1_out_14, frame_buffer_1_out_15, frame_buffer_1_out_16;
  wire [14:0] dipswitch_3_sw3;
  wire [15:0] acca_1_a_out, accb_1_b_out, instruction_register_1_always_out,
       memory_address_register_1_always_out, multiplexer_1_out, pc_1_always_out, ram_1_dout, rom_2_data,
       rom_3_data, stack_1_stack_data;

  Pull_Resistor pull_resistor_1 (.node(dipswitch_2_sw3[3]));
  DipSwitch #(.number(5)) dipswitch_1 (
    .sw1(dipswitch_3_sw3[14]), .sw2(dipswitch_3_sw3[13]), .sw3(dipswitch_3_sw3[12]),
    .sw4(dipswitch_3_sw3[11]), .sw5(dipswitch_3_sw3[10]));
  Hex_Digit_Display hex_digit_display_1 (.value(dipswitch_2_sw3));  // open: dp
  DipSwitch #(.number(7)) dipswitch_2 (
    .sw1(dipswitch_2_sw3[2]), .sw2(dipswitch_2_sw3[1]), .sw3(dipswitch_2_sw3[0]), .sw4(dipswitch_3_sw3[6]),
    .sw5(dipswitch_3_sw3[5]), .sw6(dipswitch_3_sw3[4]), .sw7(dipswitch_3_sw3[3]));
  Hex_Digit_Display hex_digit_display_2 (.value(dipswitch_3_sw3[6:3]));  // open: dp
  DipSwitch #(.number(3)) dipswitch_3 (.sw1(dipswitch_3_sw3[2]), .sw2(dipswitch_3_sw3[1]), .sw3(dipswitch_3_sw3[0]));
  buf or_1 (or_1_out, decoder_1_out6);  // OR_Gate
  not not_1 (not_1_out, clk_1_clock_out);
  Multiplexer #(.width(16)) multiplexer_1 (
    .in0({3'b000, NEGATIVE, ZERO, CARRY, instruction_register_1_always_out[14:8], step_counter_1_data_out}),
    .in1({dipswitch_2_sw3[3], dipswitch_3_sw3[14:10], dipswitch_2_sw3[2:0], dipswitch_3_sw3[6:0]}),
    .out(multiplexer_1_out), .sel(in_7));
  LED led_1 (.in(step_counter_1_data_out_2[3]));
  LED led_2 (.in(step_counter_1_data_out[2]));
  STEP_COUNTER step_counter_1 (
    .RESET(or_1_out), .CLOCK(not_1_out), .DATA_OUT({step_counter_1_data_out_2[3], step_counter_1_data_out}));
  STACK stack_1 (
    .DATA_IN({stack_1_stack_data[7:0], stack_1_stack_data[15:8]}), .CLOCK(clk_1_clock_out),
    .STACK_DATA({stack_1_stack_data[7:0], stack_1_stack_data[15:8]}));  // open: STACK_RESET, STACK_DOWN, STACK_UP, STACK_WRITE, STACK_READ
  LED led_3 (.in(step_counter_1_data_out[1]));
  LED led_4 (.in(step_counter_1_data_out[0]));
  Decoder #(.select(4)) decoder_1 (
    .out6(decoder_1_out6), .sel({step_counter_1_data_out_2[3], step_counter_1_data_out}));  // open: out0, out1, out2, out3, out4, out5, out7, out8, out9, out10, out11, out12, out13, out14, out15, en
  ROM #(.addrWidth(16), .dataWidth(16)) rom_1 (
    .addr(multiplexer_1_out),
    .data({STACK_DATA_READ, UPPER_BITS_READ, ACC_READ, CMP, SUB, ADD, STACK_UP, KB_REG_READ, READ_B, READ_Y, READ_X, INSTRUCT_READ, MAR_READ, CTN_ENB, RAM_READ_t, CTN_OUT}));
  ROM #(.addrWidth(16), .dataWidth(16)) rom_2 (.addr(multiplexer_1_out), .data(rom_2_data));
  ROM #(.addrWidth(16), .dataWidth(16)) rom_3 (.addr(multiplexer_1_out), .data(rom_3_data));
  LED led_5 (.in(memory_address_register_1_always_out[13]));
  LED led_6 (.in(memory_address_register_1_always_out[12]));
  LED led_7 (.in(memory_address_register_1_always_out[15]));
  LED led_8 (.in(memory_address_register_1_always_out[14]));
  LED led_9 (.in(memory_address_register_1_always_out[11]));
  LED led_10 (.in(memory_address_register_1_always_out[10]));
  LED led_11 (.in(memory_address_register_1_always_out[9]));
  LED led_12 (.in(memory_address_register_1_always_out[8]));
  RAM #(.addrWidth(16), .dataWidth(16), .enables("line")) ram_1 (
    .addr(memory_address_register_1_always_out), .clk(clk_1_clock_out),
    .din({stack_1_stack_data[7:0], stack_1_stack_data[15:8]}), .dout(ram_1_dout));  // open: we
  LED led_13 (.in(instruction_register_1_always_out[15]));
  LED led_14 (.in(instruction_register_1_always_out[14]));
  LED led_15 (.in(instruction_register_1_always_out[13]));
  Button button_1 (.out(button_1_out));
  LED led_16 (.in(memory_address_register_1_always_out[7]));
  LED led_17 (.in(memory_address_register_1_always_out[6]));
  LED led_18 (.in(memory_address_register_1_always_out[5]));
  LED led_19 (.in(memory_address_register_1_always_out[4]));
  LED led_20 (.in(instruction_register_1_always_out[12]));
  LED led_21 (.in(instruction_register_1_always_out[11]));
  LED led_22 (.in(instruction_register_1_always_out[10]));
  LED led_23 (.in(instruction_register_1_always_out[9]));
  Clock clock_1 (.out(clock_1_out));
  LED led_24 (.in(memory_address_register_1_always_out[3]));
  LED led_25 (.in(memory_address_register_1_always_out[2]));
  LED led_26 (.in(memory_address_register_1_always_out[1]));
  LED led_27 (.in(memory_address_register_1_always_out[0]));
  INSTRUCTION_REGISTER instruction_register_1 (
    .DATA_IN(stack_1_stack_data), .CLOCK(clk_1_clock_out), .ALWAYS_OUT(instruction_register_1_always_out),
    .DATA_OUT_LOWER(stack_1_stack_data[7:0]), .DATA_OUT_TO_UPPER(stack_1_stack_data[15:8]));  // open: WRITE, RESET, READ_TO_LOWER, READ_TO_UPPER
  LED led_28 (.in(instruction_register_1_always_out[8]));
  LED led_29 (.in(instruction_register_1_always_out[7]));
  LED led_30 (.in(instruction_register_1_always_out[6]));
  LED led_31 (.in(instruction_register_1_always_out[5]));
  CLK clk_1 (
    .CLOCK_IN(clock_1_out), .CLK_ENABLE(1'b1), .MANUAL_TICK(button_1_out), .STOP(in_1),
    .CLOCK_OUT(clk_1_clock_out));
  MEMORY_ADDRESS_REGISTER memory_address_register_1 (
    .DATA_IN({stack_1_stack_data[7:0], stack_1_stack_data[15:8]}), .MAR_IN(in_2), .CLOCK(clk_1_clock_out),
    .ALWAYS_OUT(memory_address_register_1_always_out),
    .DATA_OUT({stack_1_stack_data[7:0], stack_1_stack_data[15:8]}));  // open: MAR_OUT, MAR_RESET
  LED led_32 (.in(instruction_register_1_always_out[4]));
  LED led_33 (.in(instruction_register_1_always_out[3]));
  LED led_34 (.in(instruction_register_1_always_out[2]));
  LED led_35 (.in(instruction_register_1_always_out[1]));
  assign {stack_1_stack_data[7:0], stack_1_stack_data[15:8]} = RAM_READ ? ram_1_dout : 16'bz;  // Controlled_Buffer controlled_buffer_1
  LED led_36 (.in(instruction_register_1_always_out[0]));
  LED led_37 (.in(stack_1_stack_data[7]));
  LED led_38 (.in(stack_1_stack_data[6]));
  Pull_Resistor pull_resistor_2 (.node(stack_1_stack_data[7]));
  Pull_Resistor pull_resistor_3 (.node(stack_1_stack_data[6]));
  LED led_39 (.in(stack_1_stack_data[5]));
  LED led_40 (.in(stack_1_stack_data[4]));
  LED led_41 (.in(stack_1_stack_data[3]));
  LED led_42 (.in(stack_1_stack_data[2]));
  Pull_Resistor pull_resistor_4 (.node(stack_1_stack_data[5]));
  Pull_Resistor pull_resistor_5 (.node(stack_1_stack_data[4]));
  Pull_Resistor pull_resistor_6 (.node(stack_1_stack_data[3]));
  Pull_Resistor pull_resistor_7 (.node(stack_1_stack_data[2]));
  LED led_43 (.in(stack_1_stack_data[1]));
  LED led_44 (.in(stack_1_stack_data[0]));
  LED led_45 (.in(stack_1_stack_data[15]));
  LED led_46 (.in(stack_1_stack_data[14]));
  Pull_Resistor pull_resistor_8 (.node(stack_1_stack_data[1]));
  Pull_Resistor pull_resistor_9 (.node(stack_1_stack_data[0]));
  Pull_Resistor pull_resistor_10 (.node(stack_1_stack_data[15]));
  Pull_Resistor pull_resistor_11 (.node(stack_1_stack_data[14]));
  LED led_47 (.in(stack_1_stack_data[13]));
  LED led_48 (.in(stack_1_stack_data[12]));
  LED led_49 (.in(stack_1_stack_data[11]));
  LED led_50 (.in(stack_1_stack_data[10]));
  Pull_Resistor pull_resistor_12 (.node(stack_1_stack_data[13]));
  Pull_Resistor pull_resistor_13 (.node(stack_1_stack_data[12]));
  Pull_Resistor pull_resistor_14 (.node(stack_1_stack_data[11]));
  Pull_Resistor pull_resistor_15 (.node(stack_1_stack_data[10]));
  LED led_51 (.in(stack_1_stack_data[9]));
  LED led_52 (.in(stack_1_stack_data[8]));
  Pull_Resistor pull_resistor_16 (.node(stack_1_stack_data[9]));
  Pull_Resistor pull_resistor_17 (.node(stack_1_stack_data[8]));
  AccA acca_1 (
    .CLOCK(clk_1_clock_out), .A_IN({stack_1_stack_data[7:0], stack_1_stack_data[15:8]}),
    .A_OUT(acca_1_a_out), .A_OUT_BUS({stack_1_stack_data[7:0], stack_1_stack_data[15:8]}));  // open: A_WRITE, RESET, A_ENABLE
  X_AND_Y_REGISTER x_and_y_register_1 (
    .CLOCK(clk_1_clock_out), .X_IN({stack_1_stack_data[7:0], stack_1_stack_data[15:8]}),
    .Y_IN({stack_1_stack_data[7:0], stack_1_stack_data[15:8]}),
    .Y_OUT_BUS({stack_1_stack_data[7:0], stack_1_stack_data[15:8]}),
    .X_OUT_BUS({stack_1_stack_data[7:0], stack_1_stack_data[15:8]}));  // open: Y_ENABLE, X_WRITE, RESET, Y_WRITE, X_ENABLE
  ALU alu_1 (
    .OPCODE(in_5), .ALU_ENABLE(in_4), .A_IN(acca_1_a_out), .B_IN(accb_1_b_out),
    .DATA_OUT({stack_1_stack_data[7:0], stack_1_stack_data[15:8]}), .NEGATIVE_FLAG(alu_1_negative_flag),
    .ZERO_FLAG(alu_1_zero_flag), .CARRY_FLAG(alu_1_carry_flag));
  TTY #(.rows(12)) tty_1 (.data(stack_1_stack_data[14:8]), .clk(clk_1_clock_out), .we(undriven));  // open: clr
  Keyboard keyboard_1 (.data(keyboard_1_data));  // open: clk, re, clr, avail
  AccB accb_1 (
    .CLOCK(clk_1_clock_out), .B_IN({stack_1_stack_data[7:0], stack_1_stack_data[15:8]}),
    .B_OUT(accb_1_b_out), .B_OUT_BUS({stack_1_stack_data[7:0], stack_1_stack_data[15:8]}));  // open: B_WRITE, RESET, B_ENABLE
  PC pc_1 (
    .COUNTER_OUT(CTN_OUT), .CLOCK(clk_1_clock_out), .COUNTER_ENABLE(CTN_ENB),
    .ADDRESS_IN({stack_1_stack_data[7:0], stack_1_stack_data[15:8]}), .ALWAYS_OUT(pc_1_always_out),
    .ADDRESS_OUT({stack_1_stack_data[7:0], stack_1_stack_data[15:8]}));  // open: RESET, JUMP
  DotMatrix #(.inputtype("row"), .matrixcols(8), .matrixrows(8)) dotmatrix_1 (
    .row0(frame_buffer_1_out_9), .row1(frame_buffer_1_out_10), .row2(frame_buffer_1_out_11),
    .row3(frame_buffer_1_out_12), .row4(frame_buffer_1_out_13), .row5(frame_buffer_1_out_14),
    .row6(frame_buffer_1_out_15), .row7(frame_buffer_1_out_16));
  FRAME_BUFFER frame_buffer_1 (
    .CLOCK(clk_1_clock_out), .ADDRESS_SELECT(stack_1_stack_data[10:8]), .DATA_IN(stack_1_stack_data[15:8]),
    .out_9(frame_buffer_1_out_9), .out_10(frame_buffer_1_out_10), .out_11(frame_buffer_1_out_11),
    .out_12(frame_buffer_1_out_12), .out_13(frame_buffer_1_out_13), .out_14(frame_buffer_1_out_14),
    .out_15(frame_buffer_1_out_15), .out_16(frame_buffer_1_out_16));  // open: RESET_DISP, DATA_WRITE_EN, ADDRESS_WRITE_EN, RESET_BUFFER, UPDATE_DISP
  LED led_53 (.in(pc_1_always_out[15]));
  FLAGS flags_1 (
    .ZERO_FLAG(alu_1_zero_flag), .NEGATIVE_FLAG(alu_1_negative_flag), .CARRY_FLAG(alu_1_carry_flag),
    .CLOCK(clk_1_clock_out), .ZERO(ZERO), .NEGATIVE(NEGATIVE), .CARRY(CARRY));  // open: FLAG_ENABLE, RESET
  assign stack_1_stack_data[14:8] = KB_REG_OUT ? keyboard_1_data : 7'bz;  // Controlled_Buffer controlled_buffer_2
  LED led_54 (.in(pc_1_always_out[14]));
  LED led_55 (.in(pc_1_always_out[13]));
  LED led_56 (.in(pc_1_always_out[12]));
  LED led_57 (.in(pc_1_always_out[11]));
  LED led_58 (.in(pc_1_always_out[10]));
  LED led_59 (.in(pc_1_always_out[9]));
  LED led_60 (.in(pc_1_always_out[8]));
  LED led_61 (.in(pc_1_always_out[7]));
  LED led_62 (.in(pc_1_always_out[6]));
  LED led_63 (.in(pc_1_always_out[5]));
  LED led_64 (.in(pc_1_always_out[4]));
  LED led_65 (.in(pc_1_always_out[3]));
  LED led_66 (.in(pc_1_always_out[2]));
  LED led_67 (.in(pc_1_always_out[1]));
  LED led_68 (.in(pc_1_always_out[0]));

  // Notes on the sheet:
  //   BUS
endmodule

module ALU (
  input  [3:0] OPCODE,
  input  [15:0] A_IN,
  input  [15:0] B_IN,
  input  ALU_ENABLE,
  output NEGATIVE_FLAG,
  output CARRY_FLAG,
  output [15:0] DATA_OUT,
  output ZERO_FLAG
);

  wire comparator_1_eq, comparator_2_eq, multiplexer_2_out;
  wire [15:0] adder_1_out, and_1_out, multiplexer_1_out, multiplexer_3_out, nand_1_out, nor_1_out, not_1_out,
       or_1_out;

  assign not_1_out = ~B_IN;  // NOT_Gate not_1, 16 bits wide
  Multiplexer #(.width(16)) multiplexer_1 (.in0(B_IN), .in1(not_1_out), .out(multiplexer_1_out), .sel(comparator_1_eq));
  assign and_1_out = A_IN & B_IN;  // AND_Gate and_1, 16 bits wide
  assign or_1_out = A_IN | B_IN;  // OR_Gate or_1, 16 bits wide
  assign nand_1_out = ~(A_IN & B_IN);  // NAND_Gate nand_1, 16 bits wide
  assign nor_1_out = ~(A_IN | B_IN);  // NOR_Gate nor_1, 16 bits wide
  Multiplexer multiplexer_2 (.in0(1'b0), .in1(1'b1), .out(multiplexer_2_out), .sel(comparator_1_eq));
  Adder #(.width(16)) adder_1 (
    .a(A_IN), .b(multiplexer_1_out), .out(adder_1_out), .cin(multiplexer_2_out), .cout(CARRY_FLAG));
  Comparator #(.width(4)) comparator_1 (.a(OPCODE), .b(4'b0001), .eq(comparator_1_eq));  // open: gt, lt
  assign DATA_OUT = ALU_ENABLE ? multiplexer_3_out : 16'bz;  // Controlled_Buffer controlled_buffer_1
  Multiplexer #(.select(4), .width(16)) multiplexer_3 (
    .in0(adder_1_out), .in1(adder_1_out), .in2(and_1_out), .in3(or_1_out), .in4(nand_1_out), .in5(nor_1_out),
    .out(multiplexer_3_out));  // open: in6, in7, in8, in9, in10, in11, in12, in13, in14, in15, sel
  Comparator #(.width(16)) comparator_2 (.a(DATA_OUT), .b({16{1'b0}}), .eq(comparator_2_eq));  // open: gt, lt
  Multiplexer multiplexer_4 (.in0(1'b0), .in1(1'b1), .out(ZERO_FLAG), .sel(comparator_2_eq));

  assign NEGATIVE_FLAG = DATA_OUT[15];
endmodule

module CLK (
  input  CLOCK_IN,
  input  CLK_ENABLE,
  input  MANUAL_TICK,
  input  STOP,
  output CLOCK_OUT
);

  wire and_1_out, and_2_out, not_1_out, not_2_out, or_1_out;

  and and_1 (and_1_out, CLOCK_IN, CLK_ENABLE);
  not not_1 (not_1_out, CLK_ENABLE);
  and and_2 (and_2_out, not_1_out, MANUAL_TICK);
  not not_2 (not_2_out, STOP);
  or or_1 (or_1_out, and_1_out, and_2_out);
  and and_3 (CLOCK_OUT, or_1_out, not_2_out);
endmodule

module AccA (
  input  [15:0] A_IN,
  input  A_WRITE,
  input  CLOCK,
  input  RESET,
  input  A_ENABLE,
  output [15:0] A_OUT,
  output [15:0] A_OUT_BUS
);

  Register #(.width(16)) register_1 (.D(A_IN), .en(A_WRITE), .clk(CLOCK), .Q(A_OUT), .clr(RESET));
  assign A_OUT_BUS = A_ENABLE ? A_OUT : 16'bz;  // Controlled_Buffer controlled_buffer_1
endmodule

module AccB (
  input  [15:0] B_IN,
  input  B_WRITE,
  input  CLOCK,
  input  RESET,
  input  B_ENABLE,
  output [15:0] B_OUT,
  output [15:0] B_OUT_BUS
);

  Register #(.width(16)) register_1 (.D(B_IN), .en(B_WRITE), .clk(CLOCK), .Q(B_OUT), .clr(RESET));
  assign B_OUT_BUS = B_ENABLE ? B_OUT : 16'bz;  // Controlled_Buffer controlled_buffer_1
endmodule

module X_AND_Y_REGISTER (
  input  [15:0] X_IN,
  input  X_WRITE,
  input  CLOCK,
  input  RESET,
  input  X_ENABLE,
  input  [15:0] Y_IN,
  input  Y_WRITE,
  input  Y_ENABLE,
  output [15:0] X_OUT_BUS,
  output [15:0] Y_OUT_BUS
);

  wire [15:0] register_1_q, register_2_q;

  Register #(.width(16)) register_1 (.D(X_IN), .en(X_WRITE), .clk(CLOCK), .Q(register_1_q), .clr(RESET));
  Register #(.width(16)) register_2 (.D(Y_IN), .en(Y_WRITE), .clk(CLOCK), .Q(register_2_q), .clr(RESET));
  assign X_OUT_BUS = X_ENABLE ? register_1_q : 16'bz;  // Controlled_Buffer controlled_buffer_1
  assign Y_OUT_BUS = Y_ENABLE ? register_2_q : 16'bz;  // Controlled_Buffer controlled_buffer_2
endmodule

module FLAGS (
  input  ZERO_FLAG,
  input  NEGATIVE_FLAG,
  input  CARRY_FLAG,
  input  FLAG_ENABLE,
  input  RESET,
  input  CLOCK,
  output ZERO,
  output NEGATIVE,
  output CARRY
);

  Register #(.width(1)) register_1 (.D(ZERO_FLAG), .en(FLAG_ENABLE), .clk(CLOCK), .Q(ZERO), .clr(RESET));
  Register #(.width(1)) register_2 (.D(NEGATIVE_FLAG), .en(FLAG_ENABLE), .clk(CLOCK), .Q(NEGATIVE), .clr(RESET));
  Register #(.width(1)) register_3 (.D(CARRY_FLAG), .en(FLAG_ENABLE), .clk(CLOCK), .Q(CARRY), .clr(RESET));
endmodule

module PC (
  input  RESET,
  input  JUMP,
  input  COUNTER_ENABLE,
  input  CLOCK,
  input  [15:0] ADDRESS_IN,
  input  COUNTER_OUT,
  output [15:0] ALWAYS_OUT,
  output [15:0] ADDRESS_OUT
);

  Counter #(.max('hffff), .width(16)) counter_1 (
    .clr(RESET), .load(JUMP), .up(COUNTER_ENABLE), .count(COUNTER_ENABLE), .clk(CLOCK), .D(ADDRESS_IN),
    .Q(ALWAYS_OUT));  // open: carry
  assign ADDRESS_OUT = COUNTER_OUT ? ALWAYS_OUT : 16'bz;  // Controlled_Buffer controlled_buffer_1
endmodule

module MEMORY_ADDRESS_REGISTER (
  input  [15:0] DATA_IN,
  input  MAR_IN,
  input  MAR_OUT,
  input  CLOCK,
  input  MAR_RESET,
  output [15:0] ALWAYS_OUT,
  output [15:0] DATA_OUT
);

  Register #(.width(16)) register_1 (.D(DATA_IN), .en(MAR_IN), .clk(CLOCK), .Q(ALWAYS_OUT), .clr(MAR_RESET));
  assign DATA_OUT = MAR_OUT ? ALWAYS_OUT : 16'bz;  // Controlled_Buffer controlled_buffer_1
endmodule

module INSTRUCTION_REGISTER (
  input  [15:0] DATA_IN,
  input  WRITE,
  input  CLOCK,
  input  RESET,
  input  READ_TO_LOWER,
  input  READ_TO_UPPER,
  output [15:0] ALWAYS_OUT,
  output [7:0] DATA_OUT_TO_UPPER,
  output [7:0] DATA_OUT_LOWER
);

  Register #(.width(16)) register_1 (.D(DATA_IN), .en(WRITE), .clk(CLOCK), .Q(ALWAYS_OUT), .clr(RESET));
  assign DATA_OUT_TO_UPPER = READ_TO_UPPER ? ALWAYS_OUT[7:0] : 8'bz;  // Controlled_Buffer controlled_buffer_1
  assign DATA_OUT_LOWER = READ_TO_LOWER ? ALWAYS_OUT[7:0] : 8'bz;  // Controlled_Buffer controlled_buffer_2
endmodule

module FRAME_BUFFER (
  input  [7:0] DATA_IN,
  input  DATA_WRITE_EN,
  input  [2:0] ADDRESS_SELECT,
  input  ADDRESS_WRITE_EN,
  input  CLOCK,
  input  RESET_BUFFER,
  input  UPDATE_DISP,
  input  RESET_DISP,
  output [7:0] out_9,
  output [7:0] out_10,
  output [7:0] out_11,
  output [7:0] out_12,
  output [7:0] out_13,
  output [7:0] out_14,
  output [7:0] out_15,
  output [7:0] out_16
);

  wire demultiplexer_1_out0, demultiplexer_1_out1, demultiplexer_1_out2, demultiplexer_1_out3,
       demultiplexer_1_out4, demultiplexer_1_out5, demultiplexer_1_out6, demultiplexer_1_out7;
  wire [2:0] register_1_q;
  wire [7:0] register_2_q, register_3_q, register_4_q, register_5_q, register_6_q, register_7_q,
       register_8_q, register_9_q;

  Register #(.width(3)) register_1 (
    .D(ADDRESS_SELECT), .en(ADDRESS_WRITE_EN), .clk(CLOCK), .Q(register_1_q));  // open: clr
  Demultiplexer #(.select(3)) demultiplexer_1 (
    .out0(demultiplexer_1_out0), .out1(demultiplexer_1_out1), .out2(demultiplexer_1_out2),
    .out3(demultiplexer_1_out3), .out4(demultiplexer_1_out4), .out5(demultiplexer_1_out5),
    .out6(demultiplexer_1_out6), .out7(demultiplexer_1_out7), .in(DATA_WRITE_EN), .sel(register_1_q));
  Register register_2 (.D(DATA_IN), .en(demultiplexer_1_out0), .clk(CLOCK), .Q(register_2_q), .clr(RESET_BUFFER));
  Register register_3 (.D(DATA_IN), .en(demultiplexer_1_out1), .clk(CLOCK), .Q(register_3_q), .clr(RESET_BUFFER));
  Register register_4 (.D(DATA_IN), .en(demultiplexer_1_out2), .clk(CLOCK), .Q(register_4_q), .clr(RESET_BUFFER));
  Register register_5 (.D(DATA_IN), .en(demultiplexer_1_out3), .clk(CLOCK), .Q(register_5_q), .clr(RESET_BUFFER));
  Register register_6 (.D(DATA_IN), .en(demultiplexer_1_out4), .clk(CLOCK), .Q(register_6_q), .clr(RESET_BUFFER));
  Register register_7 (.D(DATA_IN), .en(demultiplexer_1_out5), .clk(CLOCK), .Q(register_7_q), .clr(RESET_BUFFER));
  Register register_8 (.D(DATA_IN), .en(demultiplexer_1_out6), .clk(CLOCK), .Q(register_8_q), .clr(RESET_BUFFER));
  Register register_9 (.D(DATA_IN), .en(demultiplexer_1_out7), .clk(CLOCK), .Q(register_9_q), .clr(RESET_BUFFER));
  Register register_10 (.D(register_2_q), .en(UPDATE_DISP), .clk(CLOCK), .Q(out_9), .clr(RESET_DISP));
  Register register_11 (.D(register_3_q), .en(UPDATE_DISP), .clk(CLOCK), .Q(out_10), .clr(RESET_DISP));
  Register register_12 (.D(register_4_q), .en(UPDATE_DISP), .clk(CLOCK), .Q(out_11), .clr(RESET_DISP));
  Register register_13 (.D(register_5_q), .en(UPDATE_DISP), .clk(CLOCK), .Q(out_12), .clr(RESET_DISP));
  Register register_14 (.D(register_6_q), .en(UPDATE_DISP), .clk(CLOCK), .Q(out_13), .clr(RESET_DISP));
  Register register_15 (.D(register_7_q), .en(UPDATE_DISP), .clk(CLOCK), .Q(out_14), .clr(RESET_DISP));
  Register register_16 (.D(register_8_q), .en(UPDATE_DISP), .clk(CLOCK), .Q(out_15), .clr(RESET_DISP));
  Register register_17 (.D(register_9_q), .en(UPDATE_DISP), .clk(CLOCK), .Q(out_16), .clr(RESET_DISP));
endmodule

module STEP_COUNTER (
  input  RESET,
  input  CLOCK,
  output [3:0] DATA_OUT
);

  Counter #(.max('hf), .width(4)) counter_1 (
    .clr(RESET), .up(1'b1), .count(1'b1), .clk(CLOCK), .Q(DATA_OUT));  // open: load, D, carry
endmodule

module STACK (
  input  STACK_RESET,
  input  STACK_DOWN,
  input  STACK_UP,
  input  [15:0] DATA_IN,
  input  STACK_WRITE,
  input  STACK_READ,
  input  CLOCK,
  output [15:0] STACK_DATA
);

  wire [7:0] counter_1_q;
  wire [15:0] ram_1_dout;

  Counter counter_1 (
    .clr(STACK_RESET), .up(STACK_DOWN), .count(STACK_UP), .clk(CLOCK), .Q(counter_1_q));  // open: load, D, carry
  RAM #(.dataWidth(16), .enables("line")) ram_1 (
    .addr(counter_1_q), .we(STACK_WRITE), .clk(CLOCK), .din(DATA_IN), .dout(ram_1_dout));
  assign STACK_DATA = STACK_READ ? ram_1_dout : 16'bz;  // Controlled_Buffer controlled_buffer_1
endmodule
